# Fritzing sketch fading_nodeMCU (saved by Fritzing 0.9.3b)
breadboards: 1

parts:
  U1 = NodeMCU V3.0
  LED1 = LED - 3mm [color="Red (633nm)" package="3 mm [THT]"]
  R1 = Resistor [tolerance=±5% resistance=220 package="0603 [SMD]"]
  R2 = Rotary Potentiometer (Small) [maximum_resistance=100kΩ package=THT]

nets:
  N1: U1.D1, LED1.anode
  N2: U1.3V3, R2.leg1
  N3: U1.GND#6, U1.GND#13, U1.GND#16, U1.GND#33, R1.Pin_0, R2.leg2
  N4: U1.A0, R2.wiper
  N5: LED1.cathode, R1.Pin_1

custom parts:
  NodeMCU V3.0: ESP8266 based NodeMCU
